// Digital circuit CORE.dig as structural Verilog
module CORE (
  input  clk,
  input  RST,
  input  CLR,
  input  in_4,
  input  [11:0] MIPCBI,
  input  [15:0] PCBI,
  input  MIPCBE,
  input  PCBE
);

  wire ALUD_CO, ALUDH_OE, ALUDL_OE, ALUS_OE, and_3_out, and_4_out, and_5_out, ASSERT_p5, BR_Q, button_1_out,
       CLK_t, CLKR, comparator_1_eq, comparator_1_gt, comparator_1_lt, comparator_2_eq, comparator_3_eq,
       DC_JUMP, DUMP_p5, EXT_p5, IMMED_OE, IRQ_OE, not_1_out, or_1_out, RAM_OE, RAM_WE, RF_HWE, RF_LWE,
       RF_SFR, RFSRCR_WE, ROM_OE, SFR_OE, SR_WE, WR_WE, XRAM_OE;
  wire [2:0] BR_SRC, BUS_SRC, JUMP_TYPE;
  wire [3:0] ALUSD_FUNC, multiplexer_2_out, RF_SRC;
  wire [5:4] multiplexer_2_out_2;
  wire [6:0] and_2_out;
  wire [7:0] DBUS, IMMED, RADDR, RF_Q, WR_q;
  wire [7:4] RFSRCR_q;
  wire [11:0] ADDRESS, MIPC;
  wire [15:0] pce_1_q;
  wire [47:44] DECODER_2_d;

  DCOUTER #(.generic("Bits := 12;")) dcouter_1 (
    .CLK(CLK_t), .nCLR(CLR), .CNT(1'b1), .nLE(DC_JUMP), .D(ADDRESS), .Q(MIPC));
  Comparator #(.Bits(8)) comparator_1 (
    .a(RF_Q), .b(IMMED), .gt(comparator_1_gt), .eq(comparator_1_eq), .lt(comparator_1_lt));
  Decoder #(.Selector_Bits(3)) decoder_1 (
    .sel(BUS_SRC), .out_0(ALUS_OE), .out_1(ALUDL_OE), .out_2(ALUDH_OE), .out_3(IMMED_OE), .out_4(RAM_OE),
    .out_5(XRAM_OE), .out_6(ROM_OE), .out_7(IRQ_OE));
  Multiplexer #(.Selector_Bits(3)) multiplexer_1 (
    .sel(JUMP_TYPE), .in_0(1'b0), .in_1(1'b1), .in_2(comparator_1_gt), .in_3(comparator_1_eq),
    .in_4(comparator_1_lt), .in_5(BR_Q), .in_6(RST), .in_7(1'b0), .out(DC_JUMP));
  PCE pce_1 (.CLK(CLK_t), .D(DBUS), .RS(RF_SRC), .LWE(RF_LWE), .HWE(RF_HWE), .Q(pce_1_q));
  ROM #(.AddrBits(12), .Bits(48)) DECODER_2 (
    .A(MIPC), .sel(1'b1),
    .D({DECODER_2_d, IMMED, ADDRESS, JUMP_TYPE, ALUSD_FUNC, RAM_WE, RFSRCR_WE, BR_SRC, SR_WE, WR_WE, BUS_SRC, RF_SFR, RF_HWE, RF_LWE, RF_SRC}));
  Register #(.Bits(8)) RFSRCR (.D(DBUS), .C(CLK_t), .en(RFSRCR_WE), .Q({RFSRCR_q, and_2_out[3:0]}));
  and and_1 (and_2_out[5], RFSRCR_q[4], RAM_WE);
  and and_2 (and_2_out[6], RFSRCR_q[4], RAM_OE);
  Comparator #(.Bits(12)) comparator_2 (.a(MIPCBI), .b(MIPC), .eq(comparator_2_eq));  // open: gt, lt
  Comparator #(.Bits(16)) comparator_3 (.a(PCBI), .b(pce_1_q), .eq(comparator_3_eq));  // open: gt, lt
  and and_3 (and_3_out, comparator_2_eq, MIPCBE);
  and and_4 (and_4_out, comparator_3_eq, PCBE);
  Multiplexer #(.Bits(7)) multiplexer_2 (
    .sel(RF_SFR), .in_0({1'b0, RF_HWE, RF_LWE, RF_SRC}),
    .in_1({and_2_out[6:5], and_2_out[5], and_2_out[3:0]}),
    .out({SFR_OE, multiplexer_2_out_2, multiplexer_2_out}));
  // Probe on MIPC
  // Probe on RF_SRC
  // Probe on RF_LWE
  // Probe on RF_HWE
  // Probe on RF_SFR
  // Probe on BUS_SRC
  // Probe on WR_WE
  // Probe on SR_WE
  // Probe on BR_SRC
  // Probe on RFSRCR_WE
  // Probe on RAM_WE
  // Probe on ALUSD_FUNC
  // Probe on JUMP_TYPE
  // Probe on ADDRESS
  // Probe on IMMED
  // ASSERT ASSERT: pin names not known; wires that end beside it: CLK_t, DBUS, RADDR, RAM_WE, ASSERT_p5, CLK_t
  Button button_1 (.out(button_1_out));
  reg_file RF (
    .CLK(CLK_t), .RS(multiplexer_2_out), .D(DBUS), .LLE(multiplexer_2_out_2[4]),
    .HLE(multiplexer_2_out_2[5]), .Q(RF_Q));
  BR BR (.C(CLK_t), .R(CLR), .S(BR_SRC), .ALUDF(ALUD_CO), .ALUSF(ALUD_CO), .A0(RF_Q[0]), .A7(RF_Q[7]), .Q(BR_Q));
  or or_1 (or_1_out, ASSERT_p5, and_3_out, and_4_out);
  // SwitchDT switchdt_1: pin names not known; wires that end beside it: clk, button_1_out, CLKR
  // Probe on RF_Q
  STALL STALL (.C(CLKR), .AC(or_1_out), .S(in_4), .OAC(CLK_t));  // open: G, nCLR, O
  reg__sync_clear #(.generic("Bits := 8;")) WR (.D(DBUS), .CLK(CLK_t), .CLR(CLR), .nLE(WR_WE), .Q(WR_q));
  reg__sync_clear #(.generic("Bits := 8;")) SR (.D(DBUS), .CLK(CLK_t), .CLR(CLR), .nLE(SR_WE), .Q(RADDR));
  not not_1 (not_1_out, CLK_t);
  PullDown #(.Bits(8)) pulldown_1 (.out(DBUS));
  assign DBUS = SFR_OE ? RF_Q : 8'bz;  // Driver driver_1
  // Probe on WR_q
  // Probe on RADDR
  and and_5 (and_5_out, RAM_WE, CLK_t, not_1_out);
  // Probe on DBUS
  ALU ALU (
    .A(RF_Q), .B(WR_q), .S(ALUSD_FUNC), .CI(BR_Q), .nSOE(ALUS_OE), .nDLOE(ALUDL_OE), .nDHOE(ALUDH_OE),
    .O(DBUS), .CO(ALUD_CO));
  // Probe on {RADDR, WR_q}
  ROM #(.AddrBits(16), .Bits(8)) ROM (.A({RADDR, WR_q}), .sel(ROM_OE), .D(DBUS));
  RAMSinglePortSel #(.AddrBits(7), .isProgramMemory("true"), .Bits(8)) RAM (
    .A(RADDR[6:0]), .CS(~RADDR[7]), .WE(and_5_out), .OE(RAM_OE), .D(DBUS));
  // EXTCTL EXT: pin names not known; wires that end beside it: RAM_WE, RADDR, DBUS, CLK_t, EXT_p5
  // DUMP DUMP: pin names not known; wires that end beside it: RAM_WE, RADDR, DBUS, CLK_t, DUMP_p5
  // Probe on EXT_p5
  assign DBUS = IMMED_OE ? IMMED : 8'bz;  // Driver driver_2
  // Probe on DUMP_p5

  // Other names for the same wires on the sheet: GO = in_4

  // Notes on the sheet:
  //   clk: Hz: 2147483647
  //   contents of DECODER_2 (hex, n*v repeats v):
  //   171c80488,80889,33a,85106,1c3135,1e54b8,1e08b9,8008a80000a,c004480000a,e002580000a,
  //   f001680000a,f801080040a,a00bc,80485,1a088c,236,f401380000a,f601280000a,f501380000a,
  //   f201580000a,f301580000a,f101680000a,e801e80000a,ec01b80000a,ee01a80000a,ef01a80000a,
  //   ed01b80000a,ea01d80000a,eb01d80000a,e901e80000a,e402280000a,e602180000a,e702180000a,
  //   e502280000a,e202480000a,e302480000a,e102580000a,d003580000a,d802e80000a,dc02b80000a,
  //   de02a80000a,df02a80000a,dd02b80000a,da02d80000a,db02d80000a,d902e80000a,d403280000a,
  //   d603180000a,d703180000a,d503280000a,d203480000a,d303480000a,d103580000a,c803d80000a,
  //   cc03a80000a,ce03980000a,cf03980000a,cd03a80000a,ca03c80000a,cb03c80000a,c903d80000a,
  //   c404180000a,c604080000a,c704080000a,c504180000a,c204380000a,c304380000a,c104480000a,
  //   a006780000a,b005580000a,b804e80000a,bc04b80000a,be04a80000a,bf04a80000a,bd04b80000a,
  //   ba04d80000a,bb04d80000a,b904e80000a,b405280000a,b605180000a,b705180000a,b505280000a,
  //   b205480000a,b305480000a,b105580000a,a805d80000a,ac05a80000a,ae05980000a,af05980000a,
  //   ad05a80000a,aa05c80000a,ab05c80000a,a905d80000a,a406180000a,a606080000a,a706080000a,
  //   a506180000a,a206680000a,a306680000a,3580,450b1,1592400b2,a106780000a,9006f80000a,
  //   9806980000a,9406c80000a,9606b80000a,9506c80000a,9206e80000a,9306e80000a,9106f80000a,
  //   8807780000a,8c07480000a,8e07380000a,8f07380000a,8d07480000a,8a07680000a,8b07680000a,
  //   8907780000a,8408780000a,8607a80000a,8707a80000a,8508780000a,b3c,6800c,640,a30bd,1e54b8,
  //   1e08b9,b3c,8048d,6800c,b30c0,1e54b8,1593e08b9,8208980000a,8308980000a,8108a80000a,
  //   400ea80000a,600b880000a,700a580000a,7809580000a,7c09280000a,7e09180000a,7f09180000a,
  //   7d09280000a,7a09480000a,7b09480000a,7909580000a,740a280000a,7609880000a,7709880000a,
  //   750a280000a,333c,1e54b8,1e08b9,700,6800c,8088c,b30c0,1e54b8,1593e08b9,720a480000a,
  //   730a480000a,710a580000a,680ad80000a,6c0aa80000a,6e0a980000a,6f0a980000a,6d0aa80000a,
  //   6a0ac80000a,6b0ac80000a,690ad80000a,640b580000a,660b080000a,670b080000a,650b180000a,
  //   700,30b6,1e54b8,1593e08b9,620b780000a,630b780000a,610b880000a,500cc80000a,580c180000a,
  //   5c0be80000a,5e0bd80000a,5f0bd80000a,5d0be80000a,5a0c080000a,5b0c080000a,590c180000a,
  //   540c980000a,560c480000a,570c480000a,550c580000a,700,e30b6,1e54b8,1593e08b9,520cb80000a,
  //   530cb80000a,510cc80000a,480d480000a,4c0d180000a,4e0d080000a,4f0d080000a,4d0d180000a,
  //   4a0d380000a,4b0d380000a,490d480000a,440dc80000a,460d780000a,470d780000a,450d880000a,
  //   700,c30b6,1e54b8,1593e08b9,420e980000a,430e980000a,333c,1e54b8,1e08b9,333d,1e54b8,
  //   1e08b9,80c,6800c,640,c048d,1592b00c0,410ea80000a,2012180000a,3010880000a,380f480000a,
  //   3c0f180000a,3e0f080000a,3f0f080000a,3d0f180000a,3a0f380000a,3b0f380000a,390f480000a,
  //   3410280000a,360f780000a,370f780000a,350f880000a,6005,73d,40506,a00bc,40c,1200b5,8048d,
  //   430b6,1e54b8,1593e08b9,3210780000a,3310780000a,6005,e6036,159380035,3110880000a,2811080000a,
  //   2c10d80000a,2e10c80000a,2f10c80000a,2d10d80000a,2a10f80000a,2b10f80000a,2911080000a,
  //   2411d80000a,2611380000a,2711380000a,2511480000a,273d,40506,a00bc,40c,1200b5,8048d,
  //   430b6,1e54b8,1593e08b9,2212080000a,2312080000a,1592a0036,2112180000a,1013e80000a,
  //   1812780000a,80485,1a088a,23c,15933000c,1413880000a,1612e80000a,80485,18088a,a00,23c,
  //   15933300c,1513780000a,b3c,6800c,640,a00bc,12040c,b30c0,1e54b8,1593e08b9,159320036,
  //   1213d80000a,1313d80000a,6005,c7036,159380035,1113e80000a,814380000a,80485,1a088a,
  //   23c,15931000c,415480000a,614a80000a,80485,18088a,a00,23c,15931300c,515380000a,b3c,
  //   6800c,640,a00bc,10040c,b30c0,1e54b8,1593e08b9,159300036,215780000a,315780000a,159280036,
  //   115980000a,159200000,80000880483,3bc,e04bc,100080000c,80484,1600bc,8048b,a00bd,a00be,
  //   80484,16348d,6508c,a00000,10048c,e00be,40000e,c00bb,100830,90088,100830,90089,2043c,
  //   1b9,2a00b8,1b6,1b7,1b0,1b5,1b1,1b2,1b3,1b4,1b8,1b9,1ba,171c001bb,200000
  //   contents of ROM (hex, n*v repeats v):
  //   75,81,0,75,82,0,75,83,0,75,d0,0,75,e0,0,75,f0,0,75,0,61,75,1,c6,75,2,2f,75,3,3e,75,
  //   4,f7,75,5,5b,75,6,18,75,7,80,75,8,4a,75,9,e5,75,a,b5,75,b,a9,75,c,21,75,d,c,75,e,
  //   92,75,f,68,75,10,e,75,11,11,75,12,47,75,13,13,75,14,6d,75,15,49,75,16,2c,75,17,33,
  //   75,18,f3,75,19,7a,75,1a,d9,75,1b,ae,75,1c,33,75,1d,6f,75,1e,77,75,1f,e3,75,20,cf,
  //   75,21,6c,75,22,d5,75,23,32,75,24,e7,75,25,2e,75,26,47,75,27,a8,75,28,d2,75,29,13,
  //   75,2a,6d,75,2b,ac,75,2c,55,75,2d,22,75,2e,31,75,2f,2,75,30,c6,75,31,bd,75,32,c7,75,
  //   33,2,75,34,b,75,35,74,75,36,c0,75,37,6a,75,38,74,75,39,bf,75,3a,68,75,3b,33,75,3c,
  //   ad,75,3d,11,75,3e,1c,75,3f,d4,75,40,fa,75,41,ec,75,42,14,75,43,7d,75,44,17,75,45,
  //   ee,75,46,85,75,47,a2,75,48,63,75,49,90,75,4a,7c,75,4b,d3,75,4c,41,75,4d,35,75,4e,
  //   4a,75,4f,38,75,50,28,75,51,56,75,52,87,75,53,43,75,54,9e,75,55,cc,75,56,f9,75,57,
  //   57,75,58,c3,75,59,4f,75,5a,5e,75,5b,33,75,5c,18,75,5d,8a,75,5e,2a,75,5f,93,75,60,
  //   9f,75,61,a6,75,62,eb,75,63,54,75,64,21,75,65,83,75,66,c6,75,67,15,75,68,ed,75,69,
  //   7b,75,6a,40,75,6b,4b,75,6c,72,75,6d,d8,75,6e,d0,75,6f,f,75,70,3a,75,71,a9,75,72,74,
  //   75,73,40,75,74,31,75,75,b0,75,76,56,75,77,58,75,78,13,75,79,e2,75,7a,65,75,7b,70,
  //   75,7c,de,75,7d,61,75,7e,18,75,7f,4b,75,81,38,75,82,cd,75,83,5d,75,a8,49,75,b8,a5,
  //   75,d0,c8,75,e0,5d,75,f0,20,43,0,c5,85,0,fd,75,fe,e5,75,ff,2,43,1,15,85,1,fd,75,fe,
  //   d7,75,ff,2,43,2,f,85,2,fd,75,fe,2f,75,ff,2,43,3,c1,85,3,fd,75,fe,ff,75,ff,2,43,4,
  //   d1,85,4,fd,75,fe,f7,75,ff,2,43,5,73,85,5,fd,75,fe,7b,75,ff,2,43,6,4b,85,6,fd,75,fe,
  //   5b,75,ff,2,43,7,a,85,7,fd,75,fe,8a,75,ff,2,43,8,b6,85,8,fd,75,fe,fe,75,ff,2,43,9,
  //   fe,85,9,fd,75,fe,ff,75,ff,2,43,a,3e,85,a,fd,75,fe,bf,75,ff,2,43,b,66,85,b,fd,75,fe,
  //   ef,75,ff,2,43,c,f4,85,c,fd,75,fe,f5,75,ff,2,43,d,7a,85,d,fd,75,fe,7e,75,ff,2,43,e,
  //   a7,85,e,fd,75,fe,b7,75,ff,2,43,f,6b,85,f,fd,75,fe,6b,75,ff,2,43,10,c3,85,10,fd,75,
  //   fe,cf,75,ff,2,43,11,5c,85,11,fd,75,fe,5d,75,ff,2,43,12,6a,85,12,fd,75,fe,6f,75,ff,
  //   2,43,13,94,85,13,fd,75,fe,97,75,ff,2,43,14,84,85,14,fd,75,fe,ed,75,ff,2,43,15,37,
  //   85,15,fd,75,fe,7f,75,ff,2,43,16,3d,85,16,fd,75,fe,3d,75,ff,2,43,17,56,85,17,fd,75,
  //   fe,77,75,ff,2,43,18,51,85,18,fd,75,fe,f3,75,ff,2,43,19,2a,85,19,fd,75,fe,7a,75,ff,
  //   2,43,1a,97,85,1a,fd,75,fe,df,75,ff,2,43,1b,b9,85,1b,fd,75,fe,bf,75,ff,2,43,1c,b5,
  //   85,1c,fd,75,fe,b7,75,ff,2,43,1d,1a,85,1d,fd,75,fe,7f,75,ff,2,43,1e,d0,85,1e,fd,75,
  //   fe,f7,75,ff,2,43,1f,4b,85,1f,fd,75,fe,eb,75,ff,2,43,20,c6,85,20,fd,75,fe,cf,75,ff,
  //   2,43,21,82,85,21,fd,75,fe,ee,75,ff,2,43,22,d6,85,22,fd,75,fe,d7,75,ff,2,43,23,83,
  //   85,23,fd,75,fe,b3,75,ff,2,43,24,20,85,24,fd,75,fe,e7,75,ff,2,43,25,9b,85,25,fd,75,
  //   fe,bf,75,ff,2,43,26,e1,85,26,fd,75,fe,e7,75,ff,2,43,27,91,85,27,fd,75,fe,b9,75,ff,
  //   2,43,28,e5,85,28,fd,75,fe,f7,75,ff,2,43,29,8a,85,29,fd,75,fe,9b,75,ff,2,43,2a,c5,
  //   85,2a,fd,75,fe,ed,75,ff,2,43,2b,16,85,2b,fd,75,fe,be,75,ff,2,43,2c,d6,85,2c,fd,75,
  //   fe,d7,75,ff,2,43,2d,56,85,2d,fd,75,fe,76,75,ff,2,43,2e,70,85,2e,fd,75,fe,71,75,ff,
  //   2,43,2f,99,85,2f,fd,75,fe,9b,75,ff,2,43,30,4f,85,30,fd,75,fe,cf,75,ff,2,43,31,a9,
  //   85,31,fd,75,fe,bd,75,ff,2,43,32,c7,85,32,fd,75,fe,c7,75,ff,2,43,33,2d,85,33,fd,75,
  //   fe,2f,75,ff,2,43,34,3f,85,34,fd,75,fe,3f,75,ff,2,43,35,81,85,35,fd,75,fe,f5,75,ff,
  //   2,43,36,f6,85,36,fd,75,fe,f6,75,ff,2,43,37,7a,85,37,fd,75,fe,7a,75,ff,2,43,38,b7,
  //   85,38,fd,75,fe,f7,75,ff,2,43,39,c3,85,39,fd,75,fe,ff,75,ff,2,43,3a,41,85,3a,fd,75,
  //   fe,69,75,ff,2,43,3b,f0,85,3b,fd,75,fe,f3,75,ff,2,43,3c,6a,85,3c,fd,75,fe,ef,75,ff,
  //   2,43,3d,85,85,3d,fd,75,fe,95,75,ff,2,43,3e,f6,85,3e,fd,75,fe,fe,75,ff,2,43,3f,ee,
  //   85,3f,fd,75,fe,fe,75,ff,2,43,40,3a,85,40,fd,75,fe,fa,75,ff,2,43,41,cc,85,41,fd,75,
  //   fe,ec,75,ff,2,43,42,66,85,42,fd,75,fe,76,75,ff,2,43,43,ab,85,43,fd,75,fe,ff,75,ff,
  //   2,43,44,bd,85,44,fd,75,fe,bf,75,ff,2,43,45,dd,85,45,fd,75,fe,ff,75,ff,2,43,46,fd,
  //   85,46,fd,75,fe,fd,75,ff,2,43,47,89,85,47,fd,75,fe,ab,75,ff,2,43,48,c5,85,48,fd,75,
  //   fe,e7,75,ff,2,43,49,bb,85,49,fd,75,fe,bb,75,ff,2,43,4a,db,85,4a,fd,75,fe,ff,75,ff,
  //   2,43,4b,2,85,4b,fd,75,fe,d3,75,ff,2,43,4c,99,85,4c,fd,75,fe,d9,75,ff,2,43,4d,31,85,
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endmodule
